// Logisim project 정영훈_circuit.circ as structural Verilog: 23 circuits, main circuit main
module main (
  output [12:0] out_1
);

  wire expcounter_1_levupsign, Hit, levelcounter_1_expupstop, Reset;
  wire [2:0] plussymbol_1_out_1, plussymbol_1_out_2, plussymbol_1_out_3, plussymbol_1_out_4,
       plussymbol_1_out_5;
  wire [3:0] binary_to_bcd_converter_1_p2, binary_to_bcd_converter_1_p3, binary_to_bcd_converter_1_p4,
       binary_to_bcd_converter_1_p5, Direct, Level;
  wire [8:0] ledfixedstrings_1_out_1, ledfixedstrings_1_out_2, ledfixedstrings_1_out_3,
       ledfixedstrings_1_out_4, ledfixedstrings_1_out_5;
  wire [14:0] bcdtoled_1_ledoutput, bcdtoled_2_ledoutput, bcdtoled_3_ledoutput, bcdtoled_4_ledoutput,
       bcdtoled_5_ledoutput, graphiclib_1_first, graphiclib_1_out_3, graphiclib_1_out_4, graphiclib_1_out_5,
       graphiclib_1_out_6, graphiclib_1_out_7, graphiclib_1_out_8, graphiclib_1_out_9, graphiclib_1_out_10,
       graphiclib_1_out_11, graphiclib_1_out_12, graphiclib_1_out_13, graphiclib_1_out_14,
       graphiclib_1_out_15, graphiclib_1_out_16;
  wire [49:0] directexp_1_out_2, directexp_1_out_3, directexp_1_out_4, directexp_1_out_5, directexp_1_out_6,
       expfixedshifted_1_out_1, expfixedshifted_1_out_2, expfixedshifted_1_out_3, expfixedshifted_1_out_4,
       expfixedshifted_1_out_5, extend3to50_five_1_out_6, extend3to50_five_1_out_7, extend3to50_five_1_out_8,
       extend3to50_five_1_out_9, extend3to50_five_1_out_10, extend3to50_five_2_out_6,
       extend3to50_five_2_out_7, extend3to50_five_2_out_8, extend3to50_five_2_out_9,
       extend3to50_five_2_out_10, extend3to50_five_3_out_6, extend3to50_five_3_out_7,
       extend3to50_five_3_out_8, extend3to50_five_3_out_9, extend3to50_five_3_out_10,
       extend3to50_five_4_out_6, extend3to50_five_4_out_7, extend3to50_five_4_out_8,
       extend3to50_five_4_out_9, extend3to50_five_4_out_10, extend3to50_five_5_out_6,
       extend3to50_five_5_out_7, extend3to50_five_5_out_8, extend3to50_five_5_out_9,
       extend3to50_five_5_out_10, extend3to50_five_6_out_6, extend3to50_five_6_out_7,
       extend3to50_five_6_out_8, extend3to50_five_6_out_9, extend3to50_five_6_out_10,
       extend9to50_five_1_out_6, extend9to50_five_1_out_7, extend9to50_five_1_out_8,
       extend9to50_five_1_out_9, extend9to50_five_1_out_10, leftshift_1_out_7, leftshift_1_out_8,
       leftshift_1_out_9, leftshift_1_out_10, leftshift_1_out_11, leftshift_2_out_7, leftshift_2_out_8,
       leftshift_2_out_9, leftshift_2_out_10, leftshift_2_out_11, leftshift_3_out_7, leftshift_3_out_8,
       leftshift_3_out_9, leftshift_3_out_10, leftshift_3_out_11, leftshift_4_out_7, leftshift_4_out_8,
       leftshift_4_out_9, leftshift_4_out_10, leftshift_4_out_11, leftshift_5_out_7, leftshift_5_out_8,
       leftshift_5_out_9, leftshift_5_out_10, leftshift_5_out_11, leftshift_6_out_7, leftshift_6_out_8,
       leftshift_6_out_9, leftshift_6_out_10, leftshift_6_out_11, leftshift_7_out_7, leftshift_7_out_8,
       leftshift_7_out_9, leftshift_7_out_10, leftshift_7_out_11, leftshift_8_out_7, leftshift_8_out_8,
       leftshift_8_out_9, leftshift_8_out_10, leftshift_8_out_11, leftshift_9_out_7, leftshift_9_out_8,
       leftshift_9_out_9, leftshift_9_out_10, leftshift_9_out_11, line5marge_1_p1, line5marge_1_p2,
       line5marge_1_p3, line5marge_1_p4, line5marge_1_p5, line5marge_2_p1, line5marge_2_p2, line5marge_2_p3,
       line5marge_2_p4, line5marge_2_p5, line5marge_3_p1, line5marge_3_p2, line5marge_3_p3, line5marge_3_p4,
       line5marge_3_p5, line5marge_4_p1, line5marge_4_p2, line5marge_4_p3, line5marge_4_p4, line5marge_4_p5,
       line5marge_5_p1, line5marge_5_p2, line5marge_5_p3, line5marge_5_p4, line5marge_5_p5, line5marge_6_p1,
       line5marge_6_p2, line5marge_6_p3, line5marge_6_p4, line5marge_6_p5, not_1_out, not_2_out, p1, p2, p3,
       p4, p5;

  // Binary_to_BCD_converter #(.binvalue(13)) binary_to_bcd_converter_1: pin names not known; wires that end beside it: out_1, binary_to_bcd_converter_1_p2, binary_to_bcd_converter_1_p3, binary_to_bcd_converter_1_p4, binary_to_bcd_converter_1_p5
  expCounter expcounter_1 (
    .Hit(Hit), .ExpUpstop(levelcounter_1_expupstop), .levUPsign(expcounter_1_levupsign), .ExpValue(out_1),
    .DirectRandomValue(Direct));
  BCDtoLED bcdtoled_1 (.BCDInput(binary_to_bcd_converter_1_p2), .LEDoutput(bcdtoled_1_ledoutput));
  BCDtoLED bcdtoled_2 (.BCDInput(binary_to_bcd_converter_1_p3), .LEDoutput(bcdtoled_2_ledoutput));
  BCDtoLED bcdtoled_3 (.BCDInput(binary_to_bcd_converter_1_p4), .LEDoutput(bcdtoled_3_ledoutput));
  BCDtoLED bcdtoled_4 (.BCDInput(binary_to_bcd_converter_1_p5), .LEDoutput(bcdtoled_4_ledoutput));
  Extend3to50_five extend3to50_five_1 (
    .out_6(extend3to50_five_1_out_6), .out_7(extend3to50_five_1_out_7), .out_8(extend3to50_five_1_out_8),
    .out_9(extend3to50_five_1_out_9), .out_10(extend3to50_five_1_out_10), .in_1(bcdtoled_1_ledoutput[2:0]),
    .in_2(bcdtoled_1_ledoutput[5:3]), .in_3(bcdtoled_1_ledoutput[8:6]), .in_4(bcdtoled_1_ledoutput[11:9]),
    .in_5(bcdtoled_1_ledoutput[14:12]));
  leftShift leftshift_1 (
    .out_7(leftshift_1_out_7), .out_8(leftshift_1_out_8), .out_9(leftshift_1_out_9),
    .out_10(leftshift_1_out_10), .out_11(leftshift_1_out_11), .Nshift(6'b001100),
    .in_1(extend3to50_five_1_out_6), .in_2(extend3to50_five_1_out_7), .in_4(extend3to50_five_1_out_8),
    .in_5(extend3to50_five_1_out_9), .in_6(extend3to50_five_1_out_10));
  Extend3to50_five extend3to50_five_2 (
    .out_6(extend3to50_five_2_out_6), .out_7(extend3to50_five_2_out_7), .out_8(extend3to50_five_2_out_8),
    .out_9(extend3to50_five_2_out_9), .out_10(extend3to50_five_2_out_10), .in_1(bcdtoled_2_ledoutput[2:0]),
    .in_2(bcdtoled_2_ledoutput[5:3]), .in_3(bcdtoled_2_ledoutput[8:6]), .in_4(bcdtoled_2_ledoutput[11:9]),
    .in_5(bcdtoled_2_ledoutput[14:12]));
  leftShift leftshift_2 (
    .out_7(leftshift_2_out_7), .out_8(leftshift_2_out_8), .out_9(leftshift_2_out_9),
    .out_10(leftshift_2_out_10), .out_11(leftshift_2_out_11), .Nshift(6'b001000),
    .in_1(extend3to50_five_2_out_6), .in_2(extend3to50_five_2_out_7), .in_4(extend3to50_five_2_out_8),
    .in_5(extend3to50_five_2_out_9), .in_6(extend3to50_five_2_out_10));
  Extend3to50_five extend3to50_five_3 (
    .out_6(extend3to50_five_3_out_6), .out_7(extend3to50_five_3_out_7), .out_8(extend3to50_five_3_out_8),
    .out_9(extend3to50_five_3_out_9), .out_10(extend3to50_five_3_out_10), .in_1(bcdtoled_3_ledoutput[2:0]),
    .in_2(bcdtoled_3_ledoutput[5:3]), .in_3(bcdtoled_3_ledoutput[8:6]), .in_4(bcdtoled_3_ledoutput[11:9]),
    .in_5(bcdtoled_3_ledoutput[14:12]));
  leftShift leftshift_3 (
    .out_7(leftshift_3_out_7), .out_8(leftshift_3_out_8), .out_9(leftshift_3_out_9),
    .out_10(leftshift_3_out_10), .out_11(leftshift_3_out_11), .Nshift(6'b000100),
    .in_1(extend3to50_five_3_out_6), .in_2(extend3to50_five_3_out_7), .in_4(extend3to50_five_3_out_8),
    .in_5(extend3to50_five_3_out_9), .in_6(extend3to50_five_3_out_10));
  Extend3to50_five extend3to50_five_4 (
    .out_6(extend3to50_five_4_out_6), .out_7(extend3to50_five_4_out_7), .out_8(extend3to50_five_4_out_8),
    .out_9(extend3to50_five_4_out_9), .out_10(extend3to50_five_4_out_10), .in_1(bcdtoled_4_ledoutput[2:0]),
    .in_2(bcdtoled_4_ledoutput[5:3]), .in_3(bcdtoled_4_ledoutput[8:6]), .in_4(bcdtoled_4_ledoutput[11:9]),
    .in_5(bcdtoled_4_ledoutput[14:12]));
  leftShift leftshift_4 (
    .out_7(leftshift_4_out_7), .out_8(leftshift_4_out_8), .out_9(leftshift_4_out_9),
    .out_10(leftshift_4_out_10), .out_11(leftshift_4_out_11), .Nshift({6{1'b0}}),
    .in_1(extend3to50_five_4_out_6), .in_2(extend3to50_five_4_out_7), .in_4(extend3to50_five_4_out_8),
    .in_5(extend3to50_five_4_out_9), .in_6(extend3to50_five_4_out_10));
  LEDFixedStrings ledfixedstrings_1 (
    .out_1(ledfixedstrings_1_out_1), .out_2(ledfixedstrings_1_out_2), .out_3(ledfixedstrings_1_out_3),
    .out_4(ledfixedstrings_1_out_4), .out_5(ledfixedstrings_1_out_5));
  Extend9to50_five extend9to50_five_1 (
    .out_6(extend9to50_five_1_out_6), .out_7(extend9to50_five_1_out_7), .out_8(extend9to50_five_1_out_8),
    .out_9(extend9to50_five_1_out_9), .out_10(extend9to50_five_1_out_10), .in_1(ledfixedstrings_1_out_1),
    .in_2(ledfixedstrings_1_out_2), .in_3(ledfixedstrings_1_out_3), .in_4(ledfixedstrings_1_out_4),
    .in_5(ledfixedstrings_1_out_5));
  BCDtoLED bcdtoled_5 (.BCDInput(Level), .LEDoutput(bcdtoled_5_ledoutput));
  levelCounter levelcounter_1 (
    .ResetLevel(Reset), .LevUpSign(expcounter_1_levupsign), .ExpUpstop(levelcounter_1_expupstop),
    .Level(Level));  // open: Ending
  leftShift leftshift_5 (
    .out_7(leftshift_5_out_7), .out_8(leftshift_5_out_8), .out_9(leftshift_5_out_9),
    .out_10(leftshift_5_out_10), .out_11(leftshift_5_out_11), .Nshift(6'b000100),
    .in_1(extend9to50_five_1_out_6), .in_2(extend9to50_five_1_out_7), .in_4(extend9to50_five_1_out_8),
    .in_5(extend9to50_five_1_out_9), .in_6(extend9to50_five_1_out_10));
  Extend3to50_five extend3to50_five_5 (
    .out_6(extend3to50_five_5_out_6), .out_7(extend3to50_five_5_out_7), .out_8(extend3to50_five_5_out_8),
    .out_9(extend3to50_five_5_out_9), .out_10(extend3to50_five_5_out_10), .in_1(bcdtoled_5_ledoutput[2:0]),
    .in_2(bcdtoled_5_ledoutput[5:3]), .in_3(bcdtoled_5_ledoutput[8:6]), .in_4(bcdtoled_5_ledoutput[11:9]),
    .in_5(bcdtoled_5_ledoutput[14:12]));
  line5marge line5marge_1 (
    .p1(line5marge_1_p1), .p2(line5marge_1_p2), .p3(line5marge_1_p3), .p4(line5marge_1_p4),
    .p5(line5marge_1_p5), .Obj1_Line1(leftshift_1_out_7), .in_2(leftshift_1_out_8), .in_3(leftshift_1_out_9),
    .in_4(leftshift_1_out_10), .in_5(leftshift_1_out_11), .Obj2_Line1(leftshift_2_out_7),
    .in_7(leftshift_2_out_8), .in_8(leftshift_2_out_9), .in_9(leftshift_2_out_10), .in_10(leftshift_2_out_11));
  line5marge line5marge_2 (
    .p1(line5marge_2_p1), .p2(line5marge_2_p2), .p3(line5marge_2_p3), .p4(line5marge_2_p4),
    .p5(line5marge_2_p5), .Obj1_Line1(leftshift_5_out_7), .in_2(leftshift_5_out_8), .in_3(leftshift_5_out_9),
    .in_4(leftshift_5_out_10), .in_5(leftshift_5_out_11), .Obj2_Line1(extend3to50_five_5_out_6),
    .in_7(extend3to50_five_5_out_7), .in_8(extend3to50_five_5_out_8), .in_9(extend3to50_five_5_out_9),
    .in_10(extend3to50_five_5_out_10));
  line5marge line5marge_3 (
    .p1(line5marge_3_p1), .p2(line5marge_3_p2), .p3(line5marge_3_p3), .p4(line5marge_3_p4),
    .p5(line5marge_3_p5), .Obj1_Line1(line5marge_1_p1), .in_2(line5marge_1_p2), .in_3(line5marge_1_p3),
    .in_4(line5marge_1_p4), .in_5(line5marge_1_p5), .Obj2_Line1(leftshift_3_out_7), .in_7(leftshift_3_out_8),
    .in_8(leftshift_3_out_9), .in_9(leftshift_3_out_10), .in_10(leftshift_3_out_11));
  DotMatrix #(.inputtype("row"), .matrixcols(50), .matrixrows(12)) dotmatrix_1 (
    .row0(leftshift_6_out_7), .row1(leftshift_6_out_8), .row2(leftshift_6_out_9), .row3(leftshift_6_out_10),
    .row4(leftshift_6_out_11), .row5(not_1_out), .row6(leftshift_7_out_7), .row7(leftshift_7_out_8),
    .row8(leftshift_7_out_9), .row9(leftshift_7_out_10), .row10(leftshift_7_out_11), .row11(not_2_out));
  leftShift leftshift_6 (
    .out_7(leftshift_6_out_7), .out_8(leftshift_6_out_8), .out_9(leftshift_6_out_9),
    .out_10(leftshift_6_out_10), .out_11(leftshift_6_out_11), .Nshift(6'b100100), .in_1(line5marge_2_p1),
    .in_2(line5marge_2_p2), .in_4(line5marge_2_p3), .in_5(line5marge_2_p4), .in_6(line5marge_2_p5));
  assign not_1_out = ~{50{1'b1}};  // NOT_Gate not_1, 50 bits wide
  leftShift leftshift_7 (
    .out_7(leftshift_7_out_7), .out_8(leftshift_7_out_8), .out_9(leftshift_7_out_9),
    .out_10(leftshift_7_out_10), .out_11(leftshift_7_out_11), .Nshift(6'b000110), .in_1(p1), .in_2(p2),
    .in_4(p3), .in_5(p4), .in_6(p5));
  assign not_2_out = ~{50{1'b1}};  // NOT_Gate not_2, 50 bits wide
  graphicLib graphiclib_1 (
    .Level(Level), .first(graphiclib_1_first), .out_3(graphiclib_1_out_3), .out_4(graphiclib_1_out_4),
    .out_5(graphiclib_1_out_5), .out_6(graphiclib_1_out_6), .out_7(graphiclib_1_out_7),
    .out_8(graphiclib_1_out_8), .out_9(graphiclib_1_out_9), .out_10(graphiclib_1_out_10),
    .out_11(graphiclib_1_out_11), .out_12(graphiclib_1_out_12), .out_13(graphiclib_1_out_13),
    .out_14(graphiclib_1_out_14), .out_15(graphiclib_1_out_15), .out_16(graphiclib_1_out_16));
  ExpFIXEDShifted expfixedshifted_1 (
    .out_1(expfixedshifted_1_out_1), .out_2(expfixedshifted_1_out_2), .out_3(expfixedshifted_1_out_3),
    .out_4(expfixedshifted_1_out_4), .out_5(expfixedshifted_1_out_5));
  DotMatrix #(.inputtype("row"), .matrixcols(15), .matrixrows(15)) dotmatrix_2 (
    .row0(graphiclib_1_first), .row1(graphiclib_1_out_3), .row2(graphiclib_1_out_4),
    .row3(graphiclib_1_out_5), .row4(graphiclib_1_out_6), .row5(graphiclib_1_out_7),
    .row6(graphiclib_1_out_8), .row7(graphiclib_1_out_9), .row8(graphiclib_1_out_10),
    .row9(graphiclib_1_out_11), .row10(graphiclib_1_out_12), .row11(graphiclib_1_out_13),
    .row12(graphiclib_1_out_14), .row13(graphiclib_1_out_15), .row14(graphiclib_1_out_16));
  Button button_1 (.out(Hit));
  line5marge line5marge_4 (
    .p1(line5marge_4_p1), .p2(line5marge_4_p2), .p3(line5marge_4_p3), .p4(line5marge_4_p4),
    .p5(line5marge_4_p5), .Obj1_Line1(line5marge_3_p1), .in_2(line5marge_3_p2), .in_3(line5marge_3_p3),
    .in_4(line5marge_3_p4), .in_5(line5marge_3_p5), .Obj2_Line1(leftshift_4_out_7), .in_7(leftshift_4_out_8),
    .in_8(leftshift_4_out_9), .in_9(leftshift_4_out_10), .in_10(leftshift_4_out_11));
  Button button_2 (.out(Reset));
  directExp directexp_1 (
    .out_2(directexp_1_out_2), .out_3(directexp_1_out_3), .out_4(directexp_1_out_4),
    .out_5(directexp_1_out_5), .out_6(directexp_1_out_6), .in_1(Direct));
  line5marge line5marge_5 (
    .p1(line5marge_5_p1), .p2(line5marge_5_p2), .p3(line5marge_5_p3), .p4(line5marge_5_p4),
    .p5(line5marge_5_p5), .Obj1_Line1(line5marge_4_p1), .in_2(line5marge_4_p2), .in_3(line5marge_4_p3),
    .in_4(line5marge_4_p4), .in_5(line5marge_4_p5), .Obj2_Line1(expfixedshifted_1_out_1),
    .in_7(expfixedshifted_1_out_2), .in_8(expfixedshifted_1_out_3), .in_9(expfixedshifted_1_out_4),
    .in_10(expfixedshifted_1_out_5));
  leftShift leftshift_8 (
    .out_7(leftshift_8_out_7), .out_8(leftshift_8_out_8), .out_9(leftshift_8_out_9),
    .out_10(leftshift_8_out_10), .out_11(leftshift_8_out_11), .Nshift(6'b001110), .in_1(line5marge_5_p1),
    .in_2(line5marge_5_p2), .in_4(line5marge_5_p3), .in_5(line5marge_5_p4), .in_6(line5marge_5_p5));
  plusSymbol plussymbol_1 (
    .out_1(plussymbol_1_out_1), .out_2(plussymbol_1_out_2), .out_3(plussymbol_1_out_3),
    .out_4(plussymbol_1_out_4), .out_5(plussymbol_1_out_5));
  Extend3to50_five extend3to50_five_6 (
    .out_6(extend3to50_five_6_out_6), .out_7(extend3to50_five_6_out_7), .out_8(extend3to50_five_6_out_8),
    .out_9(extend3to50_five_6_out_9), .out_10(extend3to50_five_6_out_10), .in_1(plussymbol_1_out_1),
    .in_2(plussymbol_1_out_2), .in_3(plussymbol_1_out_3), .in_4(plussymbol_1_out_4), .in_5(plussymbol_1_out_5));
  line5marge line5marge_6 (
    .p1(line5marge_6_p1), .p2(line5marge_6_p2), .p3(line5marge_6_p3), .p4(line5marge_6_p4),
    .p5(line5marge_6_p5), .Obj1_Line1(directexp_1_out_2), .in_2(directexp_1_out_3), .in_3(directexp_1_out_4),
    .in_4(directexp_1_out_5), .in_5(directexp_1_out_6), .Obj2_Line1(leftshift_8_out_7),
    .in_7(leftshift_8_out_8), .in_8(leftshift_8_out_9), .in_9(leftshift_8_out_10), .in_10(leftshift_8_out_11));
  leftShift leftshift_9 (
    .out_7(leftshift_9_out_7), .out_8(leftshift_9_out_8), .out_9(leftshift_9_out_9),
    .out_10(leftshift_9_out_10), .out_11(leftshift_9_out_11), .Nshift(6'b001001),
    .in_1(extend3to50_five_6_out_6), .in_2(extend3to50_five_6_out_7), .in_4(extend3to50_five_6_out_8),
    .in_5(extend3to50_five_6_out_9), .in_6(extend3to50_five_6_out_10));
  line5marge line5marge_7 (
    .p1(p1), .p2(p2), .p3(p3), .p4(p4), .p5(p5), .Obj1_Line1(leftshift_9_out_7), .in_2(leftshift_9_out_8),
    .in_3(leftshift_9_out_9), .in_4(leftshift_9_out_10), .in_5(leftshift_9_out_11),
    .Obj2_Line1(line5marge_6_p1), .in_7(line5marge_6_p2), .in_8(line5marge_6_p3), .in_9(line5marge_6_p4),
    .in_10(line5marge_6_p5));
endmodule

module RandomExp (
  input  Button,
  output [3:0] Randomvalue
);

  wire bit_extender_1_out, xor_1_out;
  wire [3:0] RandomExp_1_to_5_out;

  Random #(.width(4)) RandomExp_1_to_5 (.clk(Button), .out(RandomExp_1_to_5_out));  // open: clr, next
  Bit_Extender #(.in_width(4), .out_width(1), .\type ("input")) bit_extender_1 (
    .in(RandomExp_1_to_5_out), .out(bit_extender_1_out));  // open: extend
  Multiplexer #(.enable("false"), .width(4)) multiplexer_1 (
    .in0(RandomExp_1_to_5_out), .in1(4'b0001), .out(Randomvalue), .sel(xor_1_out));
  xor xor_1 (xor_1_out, bit_extender_1_out, 1'b1);
endmodule

module expCounter (
  input  Hit,
  input  ExpUpstop,
  output levUPsign,
  output [12:0] ExpValue,
  output [3:0] DirectRandomValue
);

  wire comparator_1_eq, comparator_1_gt;
  wire [12:0] adder_1_out, bit_extender_1_out;

  Register #(.width(13)) EXP (.D(adder_1_out), .en(ExpUpstop), .clk(Hit), .Q(ExpValue), .clr(levUPsign));
  assign bit_extender_1_out = {{9{1'b0}}, DirectRandomValue};  // Bit_Extender bit_extender_1
  RandomExp randomexp_1 (.Button(Hit), .Randomvalue(DirectRandomValue));
  Adder #(.width(13)) adder_1 (.a(bit_extender_1_out), .b(ExpValue), .out(adder_1_out));  // open: cin, cout
  Comparator #(.width(13)) comparator_1 (
    .a(adder_1_out), .b(13'h12c), .gt(comparator_1_gt), .eq(comparator_1_eq));  // open: lt
  or or_1 (levUPsign, comparator_1_gt, comparator_1_eq);

  // Notes on the sheet:
  //   LevelUp Exp
endmodule

module workbench (
  output [14:0] out_1,
  output [14:0] out_2,
  output [14:0] out_3,
  output [14:0] out_4,
  output [14:0] out_5,
  output [14:0] out_6,
  output [14:0] out_7,
  output [14:0] out_8,
  output [14:0] out_9,
  output [14:0] out_10,
  output [14:0] out_11,
  output [14:0] out_12,
  output [14:0] out_13,
  output [14:0] out_14,
  output [14:0] out_15
);


  assign out_1 = {15{1'b0}};
  assign out_2 = 15'h1c0;
  assign out_3 = 15'h220;
  assign out_4 = 15'h410;
  assign out_5 = 15'h410;
  assign out_6 = 15'h988;
  assign out_7 = 15'hbe8;
  assign out_8 = {15{1'b0}};
  assign out_9 = 15'h1324;
  assign out_10 = 15'h1064;
  assign out_11 = 15'h808;
  assign out_12 = 15'h888;
  assign out_13 = 15'h630;
  assign out_14 = 15'h1c0;
  assign out_15 = {15{1'b0}};

  // Notes on the sheet:
  //   EggGrapic
endmodule

module levelCounter (
  input  ResetLevel,
  input  LevUpSign,
  output ExpUpstop,
  output Ending,
  output [3:0] Level
);

  Counter #(.max('hf), .width(4)) counter_1 (
    .clr(ResetLevel), .count(ExpUpstop), .clk(LevUpSign), .carry(Ending), .Q(Level));  // open: load, up, D
  Comparator #(.width(4)) comparator_1 (.a(4'b0011), .b(Level), .gt(ExpUpstop));  // open: eq, lt
endmodule

module LEDFixedStrings (
  output [8:0] out_1,
  output [8:0] out_2,
  output [8:0] out_3,
  output [8:0] out_4,
  output [8:0] out_5
);


  assign out_1 = 9'h101;
  assign out_2 = 9'h101;
  assign out_3 = 9'h114;
  assign out_4 = 9'h115;
  assign out_5 = 9'h1c9;
endmodule

module Extend9to50_five (
  input  [8:0] in_1,
  input  [8:0] in_2,
  input  [8:0] in_3,
  input  [8:0] in_4,
  input  [8:0] in_5,
  output [49:0] out_6,
  output [49:0] out_7,
  output [49:0] out_8,
  output [49:0] out_9,
  output [49:0] out_10
);

  assign out_6 = {{41{1'b0}}, in_1};  // Bit_Extender bit_extender_1
  assign out_7 = {{41{1'b0}}, in_2};  // Bit_Extender bit_extender_2
  assign out_8 = {{41{1'b0}}, in_3};  // Bit_Extender bit_extender_3
  assign out_9 = {{41{1'b0}}, in_4};  // Bit_Extender bit_extender_4
  assign out_10 = {{41{1'b0}}, in_5};  // Bit_Extender bit_extender_5
endmodule

module leftShift (
  input  [49:0] in_1,
  input  [49:0] in_2,
  input  [5:0] Nshift,
  input  [49:0] in_4,
  input  [49:0] in_5,
  input  [49:0] in_6,
  output [49:0] out_7,
  output [49:0] out_8,
  output [49:0] out_9,
  output [49:0] out_10,
  output [49:0] out_11
);

  Shifter #(.width(50)) shifter_1 (.in(in_1), .\dist (Nshift), .out(out_7));
  Shifter #(.width(50)) shifter_2 (.in(in_2), .\dist (Nshift), .out(out_8));
  Shifter #(.width(50)) shifter_3 (.in(in_4), .\dist (Nshift), .out(out_9));
  Shifter #(.width(50)) shifter_4 (.in(in_5), .\dist (Nshift), .out(out_10));
  Shifter #(.width(50)) shifter_5 (.in(in_6), .\dist (Nshift), .out(out_11));
endmodule

module numberMatrixLib (
  output [2:0] zer,
  output [2:0] out_2,
  output [2:0] out_3,
  output [2:0] out_4,
  output [2:0] out_5,
  output [2:0] one,
  output [2:0] out_7,
  output [2:0] out_8,
  output [2:0] out_9,
  output [2:0] out_10,
  output [2:0] two,
  output [2:0] out_12,
  output [2:0] out_13,
  output [2:0] out_14,
  output [2:0] out_15,
  output [2:0] thr,
  output [2:0] out_17,
  output [2:0] out_18,
  output [2:0] out_19,
  output [2:0] out_20,
  output [2:0] four,
  output [2:0] out_22,
  output [2:0] out_23,
  output [2:0] out_24,
  output [2:0] out_25,
  output [2:0] fiv,
  output [2:0] out_27,
  output [2:0] out_28,
  output [2:0] out_29,
  output [2:0] out_30,
  output [2:0] six,
  output [2:0] out_32,
  output [2:0] out_33,
  output [2:0] out_34,
  output [2:0] out_35,
  output [2:0] sev,
  output [2:0] out_37,
  output [2:0] out_38,
  output [2:0] out_39,
  output [2:0] out_40,
  output [2:0] eight,
  output [2:0] out_42,
  output [2:0] out_43,
  output [2:0] out_44,
  output [2:0] out_45,
  output [2:0] nine,
  output [2:0] out_47,
  output [2:0] out_48,
  output [2:0] out_49,
  output [2:0] out_50
);


  assign eight = 3'b111;
  assign fiv = 3'b111;
  assign four = 3'b101;
  assign nine = 3'b111;
  assign one = 3'b010;
  assign out_2 = 3'b101;
  assign out_3 = 3'b101;
  assign out_4 = 3'b101;
  assign out_5 = 3'b111;
  assign out_7 = 3'b110;
  assign out_8 = 3'b010;
  assign out_9 = 3'b010;
  assign out_10 = 3'b111;
  assign out_12 = 3'b001;
  assign out_13 = 3'b111;
  assign out_14 = 3'b100;
  assign out_15 = 3'b111;
  assign out_17 = 3'b001;
  assign out_18 = 3'b111;
  assign out_19 = 3'b001;
  assign out_20 = 3'b111;
  assign out_22 = 3'b101;
  assign out_23 = 3'b111;
  assign out_24 = 3'b001;
  assign out_25 = 3'b001;
  assign out_27 = 3'b100;
  assign out_28 = 3'b111;
  assign out_29 = 3'b001;
  assign out_30 = 3'b111;
  assign out_32 = 3'b100;
  assign out_33 = 3'b111;
  assign out_34 = 3'b101;
  assign out_35 = 3'b111;
  assign out_37 = 3'b101;
  assign out_38 = 3'b001;
  assign out_39 = 3'b001;
  assign out_40 = 3'b001;
  assign out_42 = 3'b101;
  assign out_43 = 3'b111;
  assign out_44 = 3'b101;
  assign out_45 = 3'b111;
  assign out_47 = 3'b101;
  assign out_48 = 3'b111;
  assign out_49 = 3'b001;
  assign out_50 = 3'b111;
  assign sev = 3'b111;
  assign six = 3'b111;
  assign thr = 3'b111;
  assign two = 3'b111;
  assign zer = 3'b111;

  // Notes on the sheet:
  //   0
  //   1
  //   2
  //   3
  //   4
  //   5
  //   6
  //   7
  //   8
  //   9
endmodule

module BCDtoLED (
  input  [3:0] BCDInput,
  output [14:0] LEDoutput
);

  wire [2:0] numbermatrixlib_1_eight, numbermatrixlib_1_fiv, numbermatrixlib_1_four, numbermatrixlib_1_nine,
       numbermatrixlib_1_one, numbermatrixlib_1_out_2, numbermatrixlib_1_out_3, numbermatrixlib_1_out_4,
       numbermatrixlib_1_out_5, numbermatrixlib_1_out_7, numbermatrixlib_1_out_8, numbermatrixlib_1_out_9,
       numbermatrixlib_1_out_10, numbermatrixlib_1_out_12, numbermatrixlib_1_out_13,
       numbermatrixlib_1_out_14, numbermatrixlib_1_out_15, numbermatrixlib_1_out_17,
       numbermatrixlib_1_out_18, numbermatrixlib_1_out_19, numbermatrixlib_1_out_20,
       numbermatrixlib_1_out_22, numbermatrixlib_1_out_23, numbermatrixlib_1_out_24,
       numbermatrixlib_1_out_25, numbermatrixlib_1_out_27, numbermatrixlib_1_out_28,
       numbermatrixlib_1_out_29, numbermatrixlib_1_out_30, numbermatrixlib_1_out_32,
       numbermatrixlib_1_out_33, numbermatrixlib_1_out_34, numbermatrixlib_1_out_35,
       numbermatrixlib_1_out_37, numbermatrixlib_1_out_38, numbermatrixlib_1_out_39,
       numbermatrixlib_1_out_40, numbermatrixlib_1_out_42, numbermatrixlib_1_out_43,
       numbermatrixlib_1_out_44, numbermatrixlib_1_out_45, numbermatrixlib_1_out_47,
       numbermatrixlib_1_out_48, numbermatrixlib_1_out_49, numbermatrixlib_1_out_50, numbermatrixlib_1_sev,
       numbermatrixlib_1_six, numbermatrixlib_1_thr, numbermatrixlib_1_two, numbermatrixlib_1_zer;

  numberMatrixLib numbermatrixlib_1 (
    .zer(numbermatrixlib_1_zer), .out_2(numbermatrixlib_1_out_2), .out_3(numbermatrixlib_1_out_3),
    .out_4(numbermatrixlib_1_out_4), .out_5(numbermatrixlib_1_out_5), .one(numbermatrixlib_1_one),
    .out_7(numbermatrixlib_1_out_7), .out_8(numbermatrixlib_1_out_8), .out_9(numbermatrixlib_1_out_9),
    .out_10(numbermatrixlib_1_out_10), .two(numbermatrixlib_1_two), .out_12(numbermatrixlib_1_out_12),
    .out_13(numbermatrixlib_1_out_13), .out_14(numbermatrixlib_1_out_14), .out_15(numbermatrixlib_1_out_15),
    .thr(numbermatrixlib_1_thr), .out_17(numbermatrixlib_1_out_17), .out_18(numbermatrixlib_1_out_18),
    .out_19(numbermatrixlib_1_out_19), .out_20(numbermatrixlib_1_out_20), .four(numbermatrixlib_1_four),
    .out_22(numbermatrixlib_1_out_22), .out_23(numbermatrixlib_1_out_23), .out_24(numbermatrixlib_1_out_24),
    .out_25(numbermatrixlib_1_out_25), .fiv(numbermatrixlib_1_fiv), .out_27(numbermatrixlib_1_out_27),
    .out_28(numbermatrixlib_1_out_28), .out_29(numbermatrixlib_1_out_29), .out_30(numbermatrixlib_1_out_30),
    .six(numbermatrixlib_1_six), .out_32(numbermatrixlib_1_out_32), .out_33(numbermatrixlib_1_out_33),
    .out_34(numbermatrixlib_1_out_34), .out_35(numbermatrixlib_1_out_35), .sev(numbermatrixlib_1_sev),
    .out_37(numbermatrixlib_1_out_37), .out_38(numbermatrixlib_1_out_38), .out_39(numbermatrixlib_1_out_39),
    .out_40(numbermatrixlib_1_out_40), .eight(numbermatrixlib_1_eight), .out_42(numbermatrixlib_1_out_42),
    .out_43(numbermatrixlib_1_out_43), .out_44(numbermatrixlib_1_out_44), .out_45(numbermatrixlib_1_out_45),
    .nine(numbermatrixlib_1_nine), .out_47(numbermatrixlib_1_out_47), .out_48(numbermatrixlib_1_out_48),
    .out_49(numbermatrixlib_1_out_49), .out_50(numbermatrixlib_1_out_50));
  Multiplexer #(.enable("false"), .select(4), .width(15)) multiplexer_1 (
    .in0({numbermatrixlib_1_out_5, numbermatrixlib_1_out_4, numbermatrixlib_1_out_3, numbermatrixlib_1_out_2, numbermatrixlib_1_zer}),
    .in1({numbermatrixlib_1_out_10, numbermatrixlib_1_out_9, numbermatrixlib_1_out_8, numbermatrixlib_1_out_7, numbermatrixlib_1_one}),
    .in2({numbermatrixlib_1_out_15, numbermatrixlib_1_out_14, numbermatrixlib_1_out_13, numbermatrixlib_1_out_12, numbermatrixlib_1_two}),
    .in3({numbermatrixlib_1_out_20, numbermatrixlib_1_out_19, numbermatrixlib_1_out_18, numbermatrixlib_1_out_17, numbermatrixlib_1_thr}),
    .in4({numbermatrixlib_1_out_25, numbermatrixlib_1_out_24, numbermatrixlib_1_out_23, numbermatrixlib_1_out_22, numbermatrixlib_1_four}),
    .in5({numbermatrixlib_1_out_30, numbermatrixlib_1_out_29, numbermatrixlib_1_out_28, numbermatrixlib_1_out_27, numbermatrixlib_1_fiv}),
    .in6({numbermatrixlib_1_out_35, numbermatrixlib_1_out_34, numbermatrixlib_1_out_33, numbermatrixlib_1_out_32, numbermatrixlib_1_six}),
    .in7({numbermatrixlib_1_out_40, numbermatrixlib_1_out_39, numbermatrixlib_1_out_38, numbermatrixlib_1_out_37, numbermatrixlib_1_sev}),
    .in8({numbermatrixlib_1_out_45, numbermatrixlib_1_out_44, numbermatrixlib_1_out_43, numbermatrixlib_1_out_42, numbermatrixlib_1_eight}),
    .in9({numbermatrixlib_1_out_50, numbermatrixlib_1_out_49, numbermatrixlib_1_out_48, numbermatrixlib_1_out_47, numbermatrixlib_1_nine}),
    .out(LEDoutput), .sel(BCDInput));  // open: in10, in11, in12, in13, in14, in15
endmodule

module Extend3to50_five (
  input  [2:0] in_1,
  input  [2:0] in_2,
  input  [2:0] in_3,
  input  [2:0] in_4,
  input  [2:0] in_5,
  output [49:0] out_6,
  output [49:0] out_7,
  output [49:0] out_8,
  output [49:0] out_9,
  output [49:0] out_10
);

  assign out_6 = {{47{1'b0}}, in_1};  // Bit_Extender bit_extender_1
  assign out_7 = {{47{1'b0}}, in_2};  // Bit_Extender bit_extender_2
  assign out_8 = {{47{1'b0}}, in_3};  // Bit_Extender bit_extender_3
  assign out_9 = {{47{1'b0}}, in_4};  // Bit_Extender bit_extender_4
  assign out_10 = {{47{1'b0}}, in_5};  // Bit_Extender bit_extender_5
endmodule

module line5marge (
  input  [49:0] Obj1_Line1,
  input  [49:0] in_2,
  input  [49:0] in_3,
  input  [49:0] in_4,
  input  [49:0] in_5,
  input  [49:0] Obj2_Line1,
  input  [49:0] in_7,
  input  [49:0] in_8,
  input  [49:0] in_9,
  input  [49:0] in_10,
  output [49:0] p1,
  output [49:0] p2,
  output [49:0] p3,
  output [49:0] p4,
  output [49:0] p5
);

  assign p1 = Obj1_Line1 | Obj2_Line1;  // OR_Gate or_1, 50 bits wide
  assign p2 = in_2 | in_7;  // OR_Gate or_2, 50 bits wide
  assign p3 = in_3 | in_8;  // OR_Gate or_3, 50 bits wide
  assign p4 = in_4 | in_9;  // OR_Gate or_4, 50 bits wide
  assign p5 = in_5 | in_10;  // OR_Gate or_5, 50 bits wide

  // Other names for the same wires on the sheet: five1[49:0] = in_5; five2[49:0] = in_10; four1[49:0] = in_4;
  //   four2[49:0] = in_9; one1[49:0] = Obj1_Line1; one2[49:0] = Obj2_Line1; three1[49:0] = in_3; three2[49:0] = in_8;
  //   two1[49:0] = in_2; two2[49:0] = in_7
endmodule

module ExpFixedString (
  output [12:0] out_1,
  output [12:0] out_2,
  output [12:0] out_3,
  output [12:0] out_4,
  output [12:0] out_5
);


  assign out_1 = 13'h1d5d;
  assign out_2 = 13'h1155;
  assign out_3 = 13'h1c9c;
  assign out_4 = 13'h1151;
  assign out_5 = 13'h1d51;

  // Notes on the sheet:
  //   EXP
endmodule

module Extend13to50_five (
  input  [12:0] in_1,
  input  [12:0] in_2,
  input  [12:0] in_3,
  input  [12:0] in_4,
  input  [12:0] in_5,
  output [49:0] out_6,
  output [49:0] out_7,
  output [49:0] out_8,
  output [49:0] out_9,
  output [49:0] out_10
);

  assign out_6 = {{37{1'b0}}, in_1};  // Bit_Extender bit_extender_1
  assign out_7 = {{37{1'b0}}, in_2};  // Bit_Extender bit_extender_2
  assign out_8 = {{37{1'b0}}, in_3};  // Bit_Extender bit_extender_3
  assign out_9 = {{37{1'b0}}, in_4};  // Bit_Extender bit_extender_4
  assign out_10 = {{37{1'b0}}, in_5};  // Bit_Extender bit_extender_5
endmodule

module ExpFIXEDShifted (
  output [49:0] out_1,
  output [49:0] out_2,
  output [49:0] out_3,
  output [49:0] out_4,
  output [49:0] out_5
);

  wire [12:0] expfixedstring_1_out_1, expfixedstring_1_out_2, expfixedstring_1_out_3, expfixedstring_1_out_4,
       expfixedstring_1_out_5;
  wire [49:0] extend13to50_five_1_out_6, extend13to50_five_1_out_7, extend13to50_five_1_out_8,
       extend13to50_five_1_out_9, extend13to50_five_1_out_10;

  ExpFixedString expfixedstring_1 (
    .out_1(expfixedstring_1_out_1), .out_2(expfixedstring_1_out_2), .out_3(expfixedstring_1_out_3),
    .out_4(expfixedstring_1_out_4), .out_5(expfixedstring_1_out_5));
  Extend13to50_five extend13to50_five_1 (
    .in_1(expfixedstring_1_out_1), .in_2(expfixedstring_1_out_2), .in_3(expfixedstring_1_out_3),
    .in_4(expfixedstring_1_out_4), .in_5(expfixedstring_1_out_5), .out_6(extend13to50_five_1_out_6),
    .out_7(extend13to50_five_1_out_7), .out_8(extend13to50_five_1_out_8), .out_9(extend13to50_five_1_out_9),
    .out_10(extend13to50_five_1_out_10));
  leftShift leftshift_1 (
    .out_7(out_1), .out_8(out_2), .out_9(out_3), .out_10(out_4), .out_11(out_5), .Nshift(6'b010000),
    .in_1(extend13to50_five_1_out_6), .in_2(extend13to50_five_1_out_7), .in_4(extend13to50_five_1_out_8),
    .in_5(extend13to50_five_1_out_9), .in_6(extend13to50_five_1_out_10));
endmodule

module Extend4to50_fiveAndNshift (
  input  [3:0] in_1,
  input  [3:0] in_2,
  input  [3:0] in_3,
  input  [3:0] in_4,
  input  [3:0] in_5,
  output [49:0] out_6,
  output [49:0] out_7,
  output [49:0] out_8,
  output [49:0] out_9,
  output [49:0] out_10
);

  wire [49:0] bit_extender_1_out, bit_extender_2_out, bit_extender_3_out, bit_extender_4_out,
       bit_extender_5_out;

  assign bit_extender_1_out = {{46{1'b0}}, in_1};  // Bit_Extender bit_extender_1
  assign bit_extender_2_out = {{46{1'b0}}, in_2};  // Bit_Extender bit_extender_2
  assign bit_extender_3_out = {{46{1'b0}}, in_3};  // Bit_Extender bit_extender_3
  assign bit_extender_4_out = {{46{1'b0}}, in_4};  // Bit_Extender bit_extender_4
  assign bit_extender_5_out = {{46{1'b0}}, in_5};  // Bit_Extender bit_extender_5
  leftShift leftshift_1 (
    .out_7(out_6), .out_8(out_7), .out_9(out_8), .out_10(out_9), .out_11(out_10), .Nshift(6'b011110),
    .in_1(bit_extender_1_out), .in_2(bit_extender_2_out), .in_4(bit_extender_3_out),
    .in_5(bit_extender_4_out), .in_6(bit_extender_5_out));
endmodule

module directExp (
  input  [3:0] in_1,
  output [49:0] out_2,
  output [49:0] out_3,
  output [49:0] out_4,
  output [49:0] out_5,
  output [49:0] out_6
);

  wire [3:0] binary_to_bcd_converter_1_p2, binary_to_bcd_converter_1_p3;
  wire [14:0] bcdtoled_1_ledoutput, bcdtoled_2_ledoutput;
  wire [49:0] extend3to50_five_1_out_6, extend3to50_five_1_out_7, extend3to50_five_1_out_8,
       extend3to50_five_1_out_9, extend3to50_five_1_out_10, extend3to50_five_2_out_6,
       extend3to50_five_2_out_7, extend3to50_five_2_out_8, extend3to50_five_2_out_9,
       extend3to50_five_2_out_10, leftshift_1_out_7, leftshift_1_out_8, leftshift_1_out_9,
       leftshift_1_out_10, leftshift_1_out_11, leftshift_2_out_7, leftshift_2_out_8, leftshift_2_out_9,
       leftshift_2_out_10, leftshift_2_out_11;

  // Binary_to_BCD_converter #(.binvalue(4)) binary_to_bcd_converter_1: pin names not known; wires that end beside it: in_1, binary_to_bcd_converter_1_p2, binary_to_bcd_converter_1_p3
  BCDtoLED bcdtoled_1 (.BCDInput(binary_to_bcd_converter_1_p2), .LEDoutput(bcdtoled_1_ledoutput));
  BCDtoLED bcdtoled_2 (.BCDInput(binary_to_bcd_converter_1_p3), .LEDoutput(bcdtoled_2_ledoutput));
  Extend3to50_five extend3to50_five_1 (
    .out_6(extend3to50_five_1_out_6), .out_7(extend3to50_five_1_out_7), .out_8(extend3to50_five_1_out_8),
    .out_9(extend3to50_five_1_out_9), .out_10(extend3to50_five_1_out_10), .in_1(bcdtoled_1_ledoutput[2:0]),
    .in_2(bcdtoled_1_ledoutput[5:3]), .in_3(bcdtoled_1_ledoutput[8:6]), .in_4(bcdtoled_1_ledoutput[11:9]),
    .in_5(bcdtoled_1_ledoutput[14:12]));
  Extend3to50_five extend3to50_five_2 (
    .out_6(extend3to50_five_2_out_6), .out_7(extend3to50_five_2_out_7), .out_8(extend3to50_five_2_out_8),
    .out_9(extend3to50_five_2_out_9), .out_10(extend3to50_five_2_out_10), .in_1(bcdtoled_2_ledoutput[2:0]),
    .in_2(bcdtoled_2_ledoutput[5:3]), .in_3(bcdtoled_2_ledoutput[8:6]), .in_4(bcdtoled_2_ledoutput[11:9]),
    .in_5(bcdtoled_2_ledoutput[14:12]));
  leftShift leftshift_1 (
    .out_7(leftshift_1_out_7), .out_8(leftshift_1_out_8), .out_9(leftshift_1_out_9),
    .out_10(leftshift_1_out_10), .out_11(leftshift_1_out_11), .Nshift(6'b000100),
    .in_1(extend3to50_five_1_out_6), .in_2(extend3to50_five_1_out_7), .in_4(extend3to50_five_1_out_8),
    .in_5(extend3to50_five_1_out_9), .in_6(extend3to50_five_1_out_10));
  leftShift leftshift_2 (
    .out_7(leftshift_2_out_7), .out_8(leftshift_2_out_8), .out_9(leftshift_2_out_9),
    .out_10(leftshift_2_out_10), .out_11(leftshift_2_out_11), .in_1(extend3to50_five_2_out_6),
    .in_2(extend3to50_five_2_out_7), .in_4(extend3to50_five_2_out_8), .in_5(extend3to50_five_2_out_9),
    .in_6(extend3to50_five_2_out_10));  // open: Nshift
  line5marge line5marge_1 (
    .p1(out_2), .p2(out_3), .p3(out_4), .p4(out_5), .p5(out_6), .Obj1_Line1(leftshift_1_out_7),
    .in_2(leftshift_1_out_8), .in_3(leftshift_1_out_9), .in_4(leftshift_1_out_10), .in_5(leftshift_1_out_11),
    .Obj2_Line1(leftshift_2_out_7), .in_7(leftshift_2_out_8), .in_8(leftshift_2_out_9),
    .in_9(leftshift_2_out_10), .in_10(leftshift_2_out_11));
endmodule

module plusSymbol (
  output [2:0] out_1,
  output [2:0] out_2,
  output [2:0] out_3,
  output [2:0] out_4,
  output [2:0] out_5
);


  assign out_1 = 3'b000;
  assign out_2 = 3'b010;
  assign out_3 = 3'b111;
  assign out_4 = 3'b010;
  assign out_5 = 3'b000;
endmodule

module graphicLib (
  input  [3:0] Level,
  output [14:0] first,
  output [14:0] out_3,
  output [14:0] out_4,
  output [14:0] out_5,
  output [14:0] out_6,
  output [14:0] out_7,
  output [14:0] out_8,
  output [14:0] out_9,
  output [14:0] out_10,
  output [14:0] out_11,
  output [14:0] out_12,
  output [14:0] out_13,
  output [14:0] out_14,
  output [14:0] out_15,
  output [14:0] out_16
);

  wire Lv0, Lv1, Lv2, Lv3;
  wire [14:0] lv0graphic_1_out_1, lv0graphic_1_out_2, lv0graphic_1_out_3, lv0graphic_1_out_4,
       lv0graphic_1_out_5, lv0graphic_1_out_6, lv0graphic_1_out_7, lv0graphic_1_out_8, lv0graphic_1_out_9,
       lv0graphic_1_out_10, lv0graphic_1_out_11, lv0graphic_1_out_12, lv0graphic_1_out_13,
       lv0graphic_1_out_14, lv0graphic_1_out_15, lv1graphic_1_out_1, lv1graphic_1_out_2, lv1graphic_1_out_3,
       lv1graphic_1_out_4, lv1graphic_1_out_5, lv1graphic_1_out_6, lv1graphic_1_out_7, lv1graphic_1_out_8,
       lv1graphic_1_out_9, lv1graphic_1_out_10, lv1graphic_1_out_11, lv1graphic_1_out_12,
       lv1graphic_1_out_13, lv1graphic_1_out_14, lv1graphic_1_out_15, lv2graphic_1_out_1, lv2graphic_1_out_2,
       lv2graphic_1_out_3, lv2graphic_1_out_4, lv2graphic_1_out_5, lv2graphic_1_out_6, lv2graphic_1_out_7,
       lv2graphic_1_out_8, lv2graphic_1_out_9, lv2graphic_1_out_10, lv2graphic_1_out_11, lv2graphic_1_out_12,
       lv2graphic_1_out_13, lv2graphic_1_out_14, lv2graphic_1_out_15, lv3graphic_1_out_1, lv3graphic_1_out_2,
       lv3graphic_1_out_3, lv3graphic_1_out_4, lv3graphic_1_out_5, lv3graphic_1_out_6, lv3graphic_1_out_7,
       lv3graphic_1_out_8, lv3graphic_1_out_9, lv3graphic_1_out_10, lv3graphic_1_out_11, lv3graphic_1_out_12,
       lv3graphic_1_out_13, lv3graphic_1_out_14, lv3graphic_1_out_15;

  assign first = Lv0 ? lv0graphic_1_out_1 : 15'bz;  // Controlled_Buffer controlled_buffer_1
  Lv0Graphic lv0graphic_1 (
    .out_1(lv0graphic_1_out_1), .out_2(lv0graphic_1_out_2), .out_3(lv0graphic_1_out_3),
    .out_4(lv0graphic_1_out_4), .out_5(lv0graphic_1_out_5), .out_6(lv0graphic_1_out_6),
    .out_7(lv0graphic_1_out_7), .out_8(lv0graphic_1_out_8), .out_9(lv0graphic_1_out_9),
    .out_10(lv0graphic_1_out_10), .out_11(lv0graphic_1_out_11), .out_12(lv0graphic_1_out_12),
    .out_13(lv0graphic_1_out_13), .out_14(lv0graphic_1_out_14), .out_15(lv0graphic_1_out_15));
  assign out_3 = Lv0 ? lv0graphic_1_out_2 : 15'bz;  // Controlled_Buffer controlled_buffer_2
  assign out_4 = Lv0 ? lv0graphic_1_out_3 : 15'bz;  // Controlled_Buffer controlled_buffer_3
  assign out_5 = Lv0 ? lv0graphic_1_out_4 : 15'bz;  // Controlled_Buffer controlled_buffer_4
  assign out_6 = Lv0 ? lv0graphic_1_out_5 : 15'bz;  // Controlled_Buffer controlled_buffer_5
  assign out_7 = Lv0 ? lv0graphic_1_out_6 : 15'bz;  // Controlled_Buffer controlled_buffer_6
  assign out_8 = Lv0 ? lv0graphic_1_out_7 : 15'bz;  // Controlled_Buffer controlled_buffer_7
  assign out_9 = Lv0 ? lv0graphic_1_out_8 : 15'bz;  // Controlled_Buffer controlled_buffer_8
  assign out_10 = Lv0 ? lv0graphic_1_out_9 : 15'bz;  // Controlled_Buffer controlled_buffer_9
  assign out_11 = Lv0 ? lv0graphic_1_out_10 : 15'bz;  // Controlled_Buffer controlled_buffer_10
  assign out_12 = Lv0 ? lv0graphic_1_out_11 : 15'bz;  // Controlled_Buffer controlled_buffer_11
  assign out_13 = Lv0 ? lv0graphic_1_out_12 : 15'bz;  // Controlled_Buffer controlled_buffer_12
  assign out_14 = Lv0 ? lv0graphic_1_out_13 : 15'bz;  // Controlled_Buffer controlled_buffer_13
  assign out_15 = Lv0 ? lv0graphic_1_out_14 : 15'bz;  // Controlled_Buffer controlled_buffer_14
  assign out_16 = Lv0 ? lv0graphic_1_out_15 : 15'bz;  // Controlled_Buffer controlled_buffer_15
  assign first = Lv1 ? lv1graphic_1_out_1 : 15'bz;  // Controlled_Buffer controlled_buffer_16
  Lv1Graphic lv1graphic_1 (
    .out_1(lv1graphic_1_out_1), .out_2(lv1graphic_1_out_2), .out_3(lv1graphic_1_out_3),
    .out_4(lv1graphic_1_out_4), .out_5(lv1graphic_1_out_5), .out_6(lv1graphic_1_out_6),
    .out_7(lv1graphic_1_out_7), .out_8(lv1graphic_1_out_8), .out_9(lv1graphic_1_out_9),
    .out_10(lv1graphic_1_out_10), .out_11(lv1graphic_1_out_11), .out_12(lv1graphic_1_out_12),
    .out_13(lv1graphic_1_out_13), .out_14(lv1graphic_1_out_14), .out_15(lv1graphic_1_out_15));
  assign out_3 = Lv1 ? lv1graphic_1_out_2 : 15'bz;  // Controlled_Buffer controlled_buffer_17
  assign out_4 = Lv1 ? lv1graphic_1_out_3 : 15'bz;  // Controlled_Buffer controlled_buffer_18
  assign out_5 = Lv1 ? lv1graphic_1_out_4 : 15'bz;  // Controlled_Buffer controlled_buffer_19
  assign out_6 = Lv1 ? lv1graphic_1_out_5 : 15'bz;  // Controlled_Buffer controlled_buffer_20
  assign out_7 = Lv1 ? lv1graphic_1_out_6 : 15'bz;  // Controlled_Buffer controlled_buffer_21
  assign out_8 = Lv1 ? lv1graphic_1_out_7 : 15'bz;  // Controlled_Buffer controlled_buffer_22
  assign out_9 = Lv1 ? lv1graphic_1_out_8 : 15'bz;  // Controlled_Buffer controlled_buffer_23
  assign out_10 = Lv1 ? lv1graphic_1_out_9 : 15'bz;  // Controlled_Buffer controlled_buffer_24
  assign out_11 = Lv1 ? lv1graphic_1_out_10 : 15'bz;  // Controlled_Buffer controlled_buffer_25
  assign out_12 = Lv1 ? lv1graphic_1_out_11 : 15'bz;  // Controlled_Buffer controlled_buffer_26
  assign out_13 = Lv1 ? lv1graphic_1_out_12 : 15'bz;  // Controlled_Buffer controlled_buffer_27
  assign out_14 = Lv1 ? lv1graphic_1_out_13 : 15'bz;  // Controlled_Buffer controlled_buffer_28
  assign out_15 = Lv1 ? lv1graphic_1_out_14 : 15'bz;  // Controlled_Buffer controlled_buffer_29
  assign out_16 = Lv1 ? lv1graphic_1_out_15 : 15'bz;  // Controlled_Buffer controlled_buffer_30
  assign first = Lv2 ? lv2graphic_1_out_1 : 15'bz;  // Controlled_Buffer controlled_buffer_31
  Lv2Graphic lv2graphic_1 (
    .out_1(lv2graphic_1_out_1), .out_2(lv2graphic_1_out_2), .out_3(lv2graphic_1_out_3),
    .out_4(lv2graphic_1_out_4), .out_5(lv2graphic_1_out_5), .out_6(lv2graphic_1_out_6),
    .out_7(lv2graphic_1_out_7), .out_8(lv2graphic_1_out_8), .out_9(lv2graphic_1_out_9),
    .out_10(lv2graphic_1_out_10), .out_11(lv2graphic_1_out_11), .out_12(lv2graphic_1_out_12),
    .out_13(lv2graphic_1_out_13), .out_14(lv2graphic_1_out_14), .out_15(lv2graphic_1_out_15));
  assign out_3 = Lv2 ? lv2graphic_1_out_2 : 15'bz;  // Controlled_Buffer controlled_buffer_32
  assign out_4 = Lv2 ? lv2graphic_1_out_3 : 15'bz;  // Controlled_Buffer controlled_buffer_33
  assign out_5 = Lv2 ? lv2graphic_1_out_4 : 15'bz;  // Controlled_Buffer controlled_buffer_34
  assign out_6 = Lv2 ? lv2graphic_1_out_5 : 15'bz;  // Controlled_Buffer controlled_buffer_35
  assign out_7 = Lv2 ? lv2graphic_1_out_6 : 15'bz;  // Controlled_Buffer controlled_buffer_36
  assign out_8 = Lv2 ? lv2graphic_1_out_7 : 15'bz;  // Controlled_Buffer controlled_buffer_37
  assign out_9 = Lv2 ? lv2graphic_1_out_8 : 15'bz;  // Controlled_Buffer controlled_buffer_38
  assign out_10 = Lv2 ? lv2graphic_1_out_9 : 15'bz;  // Controlled_Buffer controlled_buffer_39
  assign out_11 = Lv2 ? lv2graphic_1_out_10 : 15'bz;  // Controlled_Buffer controlled_buffer_40
  assign out_12 = Lv2 ? lv2graphic_1_out_11 : 15'bz;  // Controlled_Buffer controlled_buffer_41
  assign out_13 = Lv2 ? lv2graphic_1_out_12 : 15'bz;  // Controlled_Buffer controlled_buffer_42
  assign out_14 = Lv2 ? lv2graphic_1_out_13 : 15'bz;  // Controlled_Buffer controlled_buffer_43
  assign out_15 = Lv2 ? lv2graphic_1_out_14 : 15'bz;  // Controlled_Buffer controlled_buffer_44
  assign out_16 = Lv2 ? lv2graphic_1_out_15 : 15'bz;  // Controlled_Buffer controlled_buffer_45
  assign first = Lv3 ? lv3graphic_1_out_1 : 15'bz;  // Controlled_Buffer controlled_buffer_46
  Lv3Graphic lv3graphic_1 (
    .out_1(lv3graphic_1_out_1), .out_2(lv3graphic_1_out_2), .out_3(lv3graphic_1_out_3),
    .out_4(lv3graphic_1_out_4), .out_5(lv3graphic_1_out_5), .out_6(lv3graphic_1_out_6),
    .out_7(lv3graphic_1_out_7), .out_8(lv3graphic_1_out_8), .out_9(lv3graphic_1_out_9),
    .out_10(lv3graphic_1_out_10), .out_11(lv3graphic_1_out_11), .out_12(lv3graphic_1_out_12),
    .out_13(lv3graphic_1_out_13), .out_14(lv3graphic_1_out_14), .out_15(lv3graphic_1_out_15));
  assign out_3 = Lv3 ? lv3graphic_1_out_2 : 15'bz;  // Controlled_Buffer controlled_buffer_47
  assign out_4 = Lv3 ? lv3graphic_1_out_3 : 15'bz;  // Controlled_Buffer controlled_buffer_48
  assign out_5 = Lv3 ? lv3graphic_1_out_4 : 15'bz;  // Controlled_Buffer controlled_buffer_49
  assign out_6 = Lv3 ? lv3graphic_1_out_5 : 15'bz;  // Controlled_Buffer controlled_buffer_50
  assign out_7 = Lv3 ? lv3graphic_1_out_6 : 15'bz;  // Controlled_Buffer controlled_buffer_51
  assign out_8 = Lv3 ? lv3graphic_1_out_7 : 15'bz;  // Controlled_Buffer controlled_buffer_52
  assign out_9 = Lv3 ? lv3graphic_1_out_8 : 15'bz;  // Controlled_Buffer controlled_buffer_53
  assign out_10 = Lv3 ? lv3graphic_1_out_9 : 15'bz;  // Controlled_Buffer controlled_buffer_54
  assign out_11 = Lv3 ? lv3graphic_1_out_10 : 15'bz;  // Controlled_Buffer controlled_buffer_55
  assign out_12 = Lv3 ? lv3graphic_1_out_11 : 15'bz;  // Controlled_Buffer controlled_buffer_56
  assign out_13 = Lv3 ? lv3graphic_1_out_12 : 15'bz;  // Controlled_Buffer controlled_buffer_57
  assign out_14 = Lv3 ? lv3graphic_1_out_13 : 15'bz;  // Controlled_Buffer controlled_buffer_58
  assign out_15 = Lv3 ? lv3graphic_1_out_14 : 15'bz;  // Controlled_Buffer controlled_buffer_59
  assign out_16 = Lv3 ? lv3graphic_1_out_15 : 15'bz;  // Controlled_Buffer controlled_buffer_60
  Demultiplexer #(.enable("false"), .select(4)) demultiplexer_1 (
    .out0(Lv0), .out1(Lv1), .out2(Lv2), .out3(Lv3), .in(1'b1), .sel(Level));  // open: out4, out5, out6, out7, out8, out9, out10, out11, out12, out13, out14, out15
endmodule

module Lv0Graphic (
  output [14:0] out_1,
  output [14:0] out_2,
  output [14:0] out_3,
  output [14:0] out_4,
  output [14:0] out_5,
  output [14:0] out_6,
  output [14:0] out_7,
  output [14:0] out_8,
  output [14:0] out_9,
  output [14:0] out_10,
  output [14:0] out_11,
  output [14:0] out_12,
  output [14:0] out_13,
  output [14:0] out_14,
  output [14:0] out_15
);


  assign out_1 = {15{1'b0}};
  assign out_2 = 15'h1c0;
  assign out_3 = 15'h220;
  assign out_4 = 15'h410;
  assign out_5 = 15'h410;
  assign out_6 = 15'h9c8;
  assign out_7 = 15'hbe8;
  assign out_8 = 15'h1324;
  assign out_9 = 15'h1064;
  assign out_10 = 15'h10c4;
  assign out_11 = 15'h808;
  assign out_12 = 15'h888;
  assign out_13 = 15'h630;
  assign out_14 = 15'h1c0;
  assign out_15 = {15{1'b0}};

  // Notes on the sheet:
  //   EggGraphic
endmodule

module Lv1Graphic (
  output [14:0] out_1,
  output [14:0] out_2,
  output [14:0] out_3,
  output [14:0] out_4,
  output [14:0] out_5,
  output [14:0] out_6,
  output [14:0] out_7,
  output [14:0] out_8,
  output [14:0] out_9,
  output [14:0] out_10,
  output [14:0] out_11,
  output [14:0] out_12,
  output [14:0] out_13,
  output [14:0] out_14,
  output [14:0] out_15
);


  assign out_1 = {15{1'b0}};
  assign out_2 = 15'h1c0;
  assign out_3 = 15'h2a0;
  assign out_4 = 15'h450;
  assign out_5 = 15'h490;
  assign out_6 = 15'h9c8;
  assign out_7 = 15'hbe8;
  assign out_8 = 15'h133c;
  assign out_9 = 15'h1064;
  assign out_10 = 15'h12c4;
  assign out_11 = 15'hc28;
  assign out_12 = 15'h898;
  assign out_13 = 15'h630;
  assign out_14 = 15'h1c0;
  assign out_15 = {15{1'b0}};

  // Notes on the sheet:
  //   Egg2Graphic
endmodule

module Lv2Graphic (
  output [14:0] out_1,
  output [14:0] out_2,
  output [14:0] out_3,
  output [14:0] out_4,
  output [14:0] out_5,
  output [14:0] out_6,
  output [14:0] out_7,
  output [14:0] out_8,
  output [14:0] out_9,
  output [14:0] out_10,
  output [14:0] out_11,
  output [14:0] out_12,
  output [14:0] out_13,
  output [14:0] out_14,
  output [14:0] out_15
);


  assign out_1 = 15'h44;
  assign out_2 = 15'haa;
  assign out_3 = 15'haa;
  assign out_4 = 15'hb2;
  assign out_5 = 15'h81;
  assign out_6 = 15'h115;
  assign out_7 = 15'h115;
  assign out_8 = 15'h701;
  assign out_9 = 15'h902;
  assign out_10 = 15'h30c4;
  assign out_11 = 15'h5008;
  assign out_12 = 15'h3608;
  assign out_13 = 15'h1128;
  assign out_14 = 15'h1128;
  assign out_15 = 15'hed8;

  // Notes on the sheet:
  //   RabbitGraphic
endmodule

module Lv3Graphic (
  output [14:0] out_1,
  output [14:0] out_2,
  output [14:0] out_3,
  output [14:0] out_4,
  output [14:0] out_5,
  output [14:0] out_6,
  output [14:0] out_7,
  output [14:0] out_8,
  output [14:0] out_9,
  output [14:0] out_10,
  output [14:0] out_11,
  output [14:0] out_12,
  output [14:0] out_13,
  output [14:0] out_14,
  output [14:0] out_15
);


  assign out_1 = 15'h44;
  assign out_2 = 15'haa;
  assign out_3 = 15'haa;
  assign out_4 = 15'hcb2;
  assign out_5 = 15'h1281;
  assign out_6 = 15'h3351;
  assign out_7 = 15'h4951;
  assign out_8 = 15'h4d01;
  assign out_9 = 15'h2302;
  assign out_10 = 15'h18c4;
  assign out_11 = 15'h1008;
  assign out_12 = 15'h1608;
  assign out_13 = 15'h1128;
  assign out_14 = 15'h1128;
  assign out_15 = 15'hed8;

  // Notes on the sheet:
  //   RabbitGraphic
endmodule
